# Fritzing sketch BhatBoard (saved by Fritzing 0.9.3b)
circuit board: 5.5cm x 3.5cm
breadboards: 1

parts:
  Step-Up_Reg = 3.3V Step-Up Breakout NCP1402 [part_number=10967]
  Xbee_S2 = XBee [part_number=XB24-Z7PIT-004]
  R1 = Resistor [tolerance=±5% resistance=30k part_number=0918-PRT package="1206 [SMD]"]
  Switch = Toggle Switch [part_number=SW873-ND package=THT]
  VCC1 = Battery [part_number=0193-PRT]

nets:
  GND: Step-Up_Reg.GND, Xbee_S2.GND, R1.Pin_0, VCC1.-
  N1: Step-Up_Reg.VOUT, Xbee_S2.VCC, Switch.2
  N2: Step-Up_Reg.VIN, VCC1.+
  N3: Xbee_S2.pin9, R1.Pin_1, Switch.1
  N4: Xbee_S2.pin17, Switch.3

notes:
  NO
  COM
  NC
  GND
  VCC
  VOUT
  VIN
  R1
  DIO3
  DTR

custom parts:
  3.3V Step-Up Breakout NCP1402: Description: The NCP1402 is a 3.3V DC-DC converter. The breakout board will accept voltage inputs between 1 and 3 Volts (such as 1 or 2 AA batteries) and output a constant, low ripple 3.3V output capable of sourcing up to 200 mA. This board is great for supplying power to 3.3V sensors or providing 3.3V from a a single AA battery. The breakout board includes the necessary peripheral components.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
  Toggle Switch: Snap Action Switch 5A (AC) Lever, Roller Actuator SPDT circuit
